# Fritzing sketch lora with esp32 connection_master (saved by Fritzing 0.9.3b)

parts:
  U1 = LuaNode32 / ESP32 [part_number=ESP32S-PIN30]
  LoRa_Module1 = Ra-01 - LoRa Module SX1278 [part_number=SX1278]

nets:
  N1: U1.D14, LoRa_Module1.RESET
  3V3: U1.3V3, LoRa_Module1.3.3V
  GND: U1.GND, LoRa_Module1.GND
  N2: U1.D2, LoRa_Module1.DIO0
  N3: U1.D5, LoRa_Module1.NSS
  N4: U1.D18, LoRa_Module1.SCK
  N5: U1.D19, LoRa_Module1.MISO
  N6: U1.D23, LoRa_Module1.MOSI

custom parts:
  LuaNode32 / ESP32: New Image for LuaNode32 DOIT ESP32 DEVKIT V1. Base parts from LuaNode32 / ESP32 ESP32 based LuaNode32 by G.Noorlander DOIT Esp32 DevKit v1 (30 pins long, 11 pins width) by Werner Rothschopf (modified by vanepp Dec 2018)
  Ra-01 - LoRa Module SX1278: The Ra-01 LoRa Module featuring the SX1278 engine by Semtech. Module by AI-Thinker. Module (Ra-01) specifications from: https://www.banggood.com/Ra-01-Smart-Electronics-SX1278-LoRa-Spread-Spectrum-Wireless-Module-Ultra-Far-10KM-433M-p-1130769.html Description: Power supply: DC1.8-3.7V(3.3V) Chip: SX1278 Frequency: 433Mhz Operating temperature: -40~+85°C On Sheild Description (may vary by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
